// Logisim project FullAdder.circ as structural Verilog: 1 circuit, main circuit main
module main (
  input  B,
  input  C_IN,
  input  A,
  output C_out,
  output sum
);

  wire and_1_out, and_2_out, xor_1_out;

  and and_1 (and_1_out, A, B);
  xor xor_1 (xor_1_out, A, B);
  and and_2 (and_2_out, C_IN, xor_1_out);
  xor xor_2 (sum, C_IN, xor_1_out);
  or or_1 (C_out, and_1_out, and_2_out);
endmodule
