# Fritzing sketch second_circute (saved by Fritzing 0.9.4)
breadboards: 1

parts:
  U1 = 74HC04_HEX_INVERTER [package=dil14]
  VCC1 = Battery
  LED1 = LED - 5mm [color="Red (633nm)" package="5 mm [THT]"]

nets:
  N1: U1.1A, U1.GND, U1.4Y, VCC1.-, LED1.cathode
  N2: U1.1Y, U1.2A
  N3: U1.2Y, U1.3A
  N4: U1.3Y, LED1.anode
  N5: U1.4A, U1.5Y
  N6: U1.5A, U1.6Y
  N7: U1.6A, U1.VCC, VCC1.+
